# Fritzing sketch circuit (saved by Fritzing 0.9.0b)
circuit board: 6.29138cm x 2.59903cm
breadboards: 1

parts:
  TMP36 = TMP36 Temperature Sensor [package="TO92 [THT]"]
  Pro_Mini_3_3V = Arduino Pro Mini v13
  FTDI = FTDI Basic Programmer

nets:
  N1: TMP36.+Vs, Pro_Mini_3_3V.VCC, FTDI.POWER
  N2: TMP36.Vout, Pro_Mini_3_3V.A0
  GND: TMP36.GND, Pro_Mini_3_3V.GND, FTDI.CTS, FTDI.GND
  N3: Pro_Mini_3_3V.DTR, FTDI.DTR
  N4: Pro_Mini_3_3V.D0/TX, FTDI.RXI
  N5: Pro_Mini_3_3V.D1/RX, FTDI.TXO
